# Fritzing sketch 8x3valveModule_1.0 (saved by Fritzing 0.9.3b)
circuit board: 2.20351cm x 4.63993cm
breadboards: 1

parts:
  J1 = female pin header, 2 pins [form="♀ (female)"]
  J3 = female pin header, 2 pins [form="♀ (female)"]
  J4 = female pin header, 2 pins [form="♀ (female)"]
  J5 = female pin header, 2 pins [form="♀ (female)"]
  J7 = female pin header, 2 pins [form="♀ (female)"]
  J8 = female pin header, 2 pins [form="♀ (female)"]
  J9 = female pin header, 2 pins [form="♀ (female)"]
  J10 = female pin header, 2 pins [form="♀ (female)"]
  J13 = female pin header, 2 pins [form="♀ (female)"]
  J14 = female pin header, 2 pins [form="♀ (female)"]
  J15 = female pin header, 2 pins [form="♀ (female)"]
  J16 = female pin header, 2 pins [form="♀ (female)"]
  J17 = female pin header, 2 pins [form="♀ (female)"]
  J18 = female pin header, 2 pins [form="♀ (female)"]
  J19 = female pin header, 2 pins [form="♀ (female)"]
  J20 = female pin header, 2 pins [form="♀ (female)"]
  J25 = female pin header, 2 pins [form="♀ (female)"]
  J26 = female pin header, 2 pins [form="♀ (female)"]
  J27 = female pin header, 2 pins [form="♀ (female)"]
  J28 = female pin header, 2 pins [form="♀ (female)"]
  J29 = female pin header, 2 pins [form="♀ (female)"]
  J30 = female pin header, 2 pins [form="♀ (female)"]
  J31 = female pin header, 2 pins [form="♀ (female)"]
  J32 = female pin header, 2 pins [form="♀ (female)"]
  R1 = Resistor [tolerance=±5% resistance=220 package=THT]
  J33 = double row female pin header, 16 pins [form="♀ (female)"]
  LED1 = LED - 3mm [color="Red (633nm)" package="3 mm [THT]"]
  J35 = double row female pin header, 2 pins [form="♀ (female)"]
  1 = LED - 3mm [color="Red (633nm)" package="3 mm [THT]"]
  2 = LED - 3mm [color="Red (633nm)" package="3 mm [THT]"]
  3 = LED - 3mm [color="Red (633nm)" package="3 mm [THT]"]
  4 = LED - 3mm [color="Red (633nm)" package="3 mm [THT]"]
  5 = LED - 3mm [color="Red (633nm)" package="3 mm [THT]"]
  6 = LED - 3mm [color="Red (633nm)" package="3 mm [THT]"]
  7 = LED - 3mm [color="Red (633nm)" package="3 mm [THT]"]
  8 = LED - 3mm [color="Red (633nm)" package="3 mm [THT]"]

nets:
  N1: J1.pin1, J3.pin1, J4.pin1, J33.pin1, 8.cathode
  N2: J1.pin2, J3.pin2, J4.pin2, J5.pin2, J7.pin2, J8.pin2, J9.pin2, J10.pin2, J13.pin2, J14.pin2, J15.pin2, J16.pin2, J17.pin2, J18.pin2, J19.pin2, J20.pin2, J25.pin2, J26.pin2, J27.pin2, J28.pin2, J29.pin2, J30.pin2, J31.pin2, J32.pin2, R1.Pin_1, J33.pin9, J33.pin10, J33.pin11, J33.pin12, J33.pin13, J33.pin14, J33.pin15, J33.pin16, J35.pin1
  N3: J5.pin1, J7.pin1, J8.pin1, J33.pin2, 7.cathode
  N4: J9.pin1, J13.pin1, J16.pin1, J33.pin4, 5.cathode
  N5: J10.pin1, J14.pin1, J15.pin1, J33.pin3, 6.cathode
  N6: J17.pin1, J28.pin1, J32.pin1, J33.pin6, 3.cathode
  N7: J18.pin1, J26.pin1, J31.pin1, J33.pin8, 1.cathode
  N8: J19.pin1, J25.pin1, J30.pin1, J33.pin5, 4.cathode
  N9: J20.pin1, J27.pin1, J29.pin1, J33.pin7, 2.cathode
  N10: R1.Pin_0, LED1.anode, 1.anode, 2.anode, 3.anode, 4.anode, 5.anode, 6.anode, 7.anode, 8.anode
  N11: LED1.cathode, J35.pin2

notes:
  12V
  +
  -
  IsWISaS_8x3valveModule_1.0
  https://github.com/stseeger/IsWISaS
  GND
