# Fritzing sketch Controller_A1.0 (saved by Fritzing 0.9.3b)
circuit board: 4.90417cm x 5.3cm
breadboards: 1

parts:
  Arduino_Nano = Arduino Nano (Rev3.0)
  J1 = Power Jack [package=power_jack_pth_lock]
  ULN2803A = ULN2803A [package=THT]
  8 = female pin header, 2 pins [form="♀ (female)"]
  1 = female pin header, 2 pins [form="♀ (female)"]
  2 = female pin header, 2 pins [form="♀ (female)"]
  3 = female pin header, 2 pins [form="♀ (female)"]
  4 = female pin header, 2 pins [form="♀ (female)"]
  5 = female pin header, 2 pins [form="♀ (female)"]
  6 = female pin header, 2 pins [form="♀ (female)"]
  7 = female pin header, 2 pins [form="♀ (female)"]
  PS/2_port_B2 = mini DIN 6 Connector [package=mini-din6]
  C2 = Electrolytic Capacitor [capacitance=100µF package="100 mil [THT, electrolytic]"]
  R4 = Resistor [tolerance=±5% resistance=100k package=THT]
  R1 = Resistor [tolerance=±5% resistance=1k package=THT]
  PS/2_port_B3 = mini DIN 6 Connector [package=mini-din6]
  C1 = Electrolytic Capacitor [capacitance=100µF package="100 mil [THT, electrolytic]"]
  R3 = Resistor [tolerance=±5% resistance=100k package=THT]
  R2 = Resistor [tolerance=±5% resistance=1k package=THT]
  ULN2803A_2 = ULN2803A [package=THT]
  15 = female pin header, 2 pins [form="♀ (female)"]
  14 = female pin header, 2 pins [form="♀ (female)"]
  13 = female pin header, 2 pins [form="♀ (female)"]
  12 = female pin header, 2 pins [form="♀ (female)"]
  11 = female pin header, 2 pins [form="♀ (female)"]
  10 = female pin header, 2 pins [form="♀ (female)"]
  9 = female pin header, 2 pins [form="♀ (female)"]
  16 = female pin header, 2 pins [form="♀ (female)"]
  8_2 = female pin header, 2 pins [form="♀ (female)"]
  16_2 = female pin header, 2 pins [form="♀ (female)"]

nets:
  GND: Arduino_Nano.GND, J1.GND, J1.GNDBREAK, ULN2803A.0V, PS/2_port_B2.2, PS/2_port_B2.6, C2.-, R4.Pin_1, PS/2_port_B3.2, PS/2_port_B3.6, C1.-, R3.Pin_1, ULN2803A_2.0V, 8_2.pin2, 16_2.pin2
  N1: Arduino_Nano.D2, ULN2803A.In_8
  N2: Arduino_Nano.D3, ULN2803A.In_7
  N3: Arduino_Nano.D4, ULN2803A.In_6
  N4: Arduino_Nano.D5, R1.Pin_0
  N5: Arduino_Nano.D6, R2.Pin_0
  N6: Arduino_Nano.D7, ULN2803A.In_3
  N7: Arduino_Nano.D8, ULN2803A.In_2
  N8: Arduino_Nano.D9, ULN2803A.In_1
  N9: Arduino_Nano.D10, ULN2803A.In_4
  N10: Arduino_Nano.D11/MOSI, ULN2803A.In_5
  N11: Arduino_Nano.D12/MISO, ULN2803A_2.In_2
  N12: Arduino_Nano.A7, ULN2803A_2.In_3
  N13: Arduino_Nano.A6, ULN2803A_2.In_4
  N14: Arduino_Nano.A5, ULN2803A_2.In_5
  N15: Arduino_Nano.A4, ULN2803A_2.In_6
  N16: Arduino_Nano.A3, ULN2803A_2.In_7
  N17: Arduino_Nano.A2, ULN2803A_2.In_8
  N18: Arduino_Nano.A1, PS/2_port_B2.5, R4.Pin_0
  N19: Arduino_Nano.A0, PS/2_port_B3.5, R3.Pin_0
  N20: Arduino_Nano.D13/SCK, ULN2803A_2.In_1
  N21: J1.PWR, ULN2803A.COM_-_Common, 8.pin1, 1.pin1, 2.pin1, 3.pin1, 4.pin1, 5.pin1, 6.pin1, 7.pin1, PS/2_port_B2.1, PS/2_port_B2.4, PS/2_port_B3.1, PS/2_port_B3.4, ULN2803A_2.COM_-_Common, 15.pin1, 14.pin1, 13.pin1, 12.pin1, 11.pin1, 10.pin1, 9.pin1, 16.pin1, 8_2.pin1, 16_2.pin1
  N22: ULN2803A.Out_8, 8.pin2
  N23: ULN2803A.Out_7, 7.pin2
  N24: ULN2803A.Out_6, 6.pin2
  N25: ULN2803A.Out_5, 5.pin2
  N26: ULN2803A.Out_4, 4.pin2
  N27: ULN2803A.Out_3, 3.pin2
  N28: ULN2803A.Out_2, 2.pin2
  N29: ULN2803A.Out_1, 1.pin2
  N30: PS/2_port_B2.3, C2.+, R2.Pin_1
  N31: R1.Pin_1, PS/2_port_B3.3, C1.+
  N32: ULN2803A_2.Out_8, 16.pin2
  N33: ULN2803A_2.Out_7, 15.pin2
  N34: ULN2803A_2.Out_6, 14.pin2
  N35: ULN2803A_2.Out_5, 13.pin2
  N36: ULN2803A_2.Out_4, 12.pin2
  N37: ULN2803A_2.Out_3, 11.pin2
  N38: ULN2803A_2.Out_2, 10.pin2
  N39: ULN2803A_2.Out_1, 9.pin2

notes:
  VDC
  +
  1-8
  A  B
  IsWISaS_Controller_A1.0
  https://github.com/stseeger/IsWISaS
  GND
  9-16

// code stored in the sketch: 16ValveControllerBoard_v1.ino
#include <Cmd.h>

#define POWER_PIN D10
#define VALVECOUNT 16

const byte valvePins[16] = {D2, D3, D4, D5, D6, D7, D8, D9, A7, A6, A5, A4, A3, A2, A1, A0};

byte activeValve = 0;

void identify(int arg_cnt, char **args){
  Serial.print("deviceType:");
  arg_cnt==1 ? Serial.print(' ') : Serial.println();
  Serial.println("ValveController");
}

void cmd_open(int arg_cnt, char **args){
  int valveNumber = cmdStr2Num(args[1], 10);  
  activate(valveNumber);
}

void activate(byte n){
  n = n > 0 & n <=17 ? n : 1;
	activeValve = n;
	Serial.print("open valve ");
	Serial.println(n);
  for(byte i=0; i<VALVECOUNT; i++){
    digitalWrite(valvePins[i], i==(n-1));    
  } 
}

void setup() {
  cmdInit(9600);
  cmdAdd("?", identify);
  cmdAdd("open", cmd_open);
    
	for(byte i=0; i<VALVECOUNT; i++){
    pinMode(valvePins[i], OUTPUT);
    digitalWrite(valvePins[i], LOW);    
  }

  pinMode(POWER_PIN, OUTPUT);
  digitalWrite(POWER_PIN, HIGH);
}

void loop(){
	cmdPoll();	
}
