# Fritzing sketch Controller_B1.0 (saved by Fritzing 0.9.3b)
circuit board: 4.2356cm x 5.51277cm
breadboards: 1

parts:
  RX0_TX1 = Arduino Nano (Rev3.0)
  PS/2_port_B2 = mini DIN 6 Connector [package=mini-din6]
  C2 = Electrolytic Capacitor [capacitance=100µF package="100 mil [THT, electrolytic]"]
  R4 = Resistor [tolerance=±5% resistance=100k package=THT]
  R1 = Resistor [tolerance=±5% resistance=1k package=THT]
  PS/2_port_B3 = mini DIN 6 Connector [package=mini-din6]
  C1 = Electrolytic Capacitor [capacitance=100µF package="100 mil [THT, electrolytic]"]
  R2 = Resistor [tolerance=±5% resistance=1k package=THT]
  J2 = Power Jack [package=power_jack_pth_lock]
  R3 = Resistor [tolerance=±5% resistance=100k package=THT]
  U2 = RJ45 Jack [package=rj45-8]
  ULN2803A = ULN2803A [package=THT]
  8 = female pin header, 2 pins [form="♀ (female)"]
  8_2 = female pin header, 2 pins [form="♀ (female)"]
  8_3 = female pin header, 2 pins [form="♀ (female)"]
  8_4 = female pin header, 2 pins [form="♀ (female)"]
  8_5 = female pin header, 2 pins [form="♀ (female)"]
  8_6 = female pin header, 2 pins [form="♀ (female)"]
  8_7 = female pin header, 2 pins [form="♀ (female)"]
  8_8 = female pin header, 2 pins [form="♀ (female)"]

nets:
  GND: RX0_TX1.GND, PS/2_port_B2.2, PS/2_port_B2.6, C2.-, R4.Pin_1, PS/2_port_B3.2, PS/2_port_B3.6, C1.-, J2.GND, J2.GNDBREAK, R3.Pin_1, U2.7, ULN2803A.0V
  N1: RX0_TX1.D2, ULN2803A.In_8
  N2: RX0_TX1.D3, ULN2803A.In_7
  N3: RX0_TX1.D4, ULN2803A.In_6
  N4: RX0_TX1.D5, R1.Pin_0
  N5: RX0_TX1.D6, R2.Pin_0
  N6: RX0_TX1.D7, ULN2803A.In_3
  N7: RX0_TX1.D8, ULN2803A.In_2
  N8: RX0_TX1.D9, ULN2803A.In_1
  N9: RX0_TX1.D10, ULN2803A.In_4
  N10: RX0_TX1.D11/MOSI, ULN2803A.In_5
  N11: RX0_TX1.5V, U2.5, U2.6
  N12: RX0_TX1.A7, PS/2_port_B2.5, R4.Pin_0
  N13: RX0_TX1.A6, PS/2_port_B3.5, R3.Pin_0
  N14: RX0_TX1.A5, U2.4
  N15: RX0_TX1.A4, U2.2
  N16: RX0_TX1.A3, U2.1
  N17: RX0_TX1.A2, U2.3
  N18: PS/2_port_B2.1, PS/2_port_B2.4, PS/2_port_B3.1, PS/2_port_B3.4, J2.PWR, U2.8, ULN2803A.COM_-_Common, 8.pin1, 8_2.pin1, 8_3.pin1, 8_4.pin1, 8_5.pin1, 8_6.pin1, 8_7.pin1, 8_8.pin1
  N19: PS/2_port_B2.3, C2.+, R2.Pin_1
  N20: R1.Pin_1, PS/2_port_B3.3, C1.+
  N21: ULN2803A.Out_8, 8.pin2
  N22: ULN2803A.Out_7, 8_2.pin2
  N23: ULN2803A.Out_6, 8_3.pin2
  N24: ULN2803A.Out_5, 8_4.pin2
  N25: ULN2803A.Out_4, 8_5.pin2
  N26: ULN2803A.Out_3, 8_6.pin2
  N27: ULN2803A.Out_2, 8_7.pin2
  N28: ULN2803A.Out_1, 8_8.pin2

notes:
  +
  IsWISaS_Controller_B1.0
  https://github.com/stseeger/IsWISaS
  extension B ->
  1
  8

// code stored in the sketch: 16ValveControllerBoard_v1.ino
#include <Cmd.h>

#define POWER_PIN D10
#define VALVECOUNT 16

const byte valvePins[16] = {D2, D3, D4, D5, D6, D7, D8, D9, A7, A6, A5, A4, A3, A2, A1, A0};

byte activeValve = 0;

void identify(int arg_cnt, char **args){
  Serial.print("deviceType:");
  arg_cnt==1 ? Serial.print(' ') : Serial.println();
  Serial.println("ValveController");
}

void cmd_open(int arg_cnt, char **args){
  int valveNumber = cmdStr2Num(args[1], 10);  
  activate(valveNumber);
}

void activate(byte n){
  n = n > 0 & n <=17 ? n : 1;
	activeValve = n;
	Serial.print("open valve ");
	Serial.println(n);
  for(byte i=0; i<VALVECOUNT; i++){
    digitalWrite(valvePins[i], i==(n-1));    
  } 
}

void setup() {
  cmdInit(9600);
  cmdAdd("?", identify);
  cmdAdd("open", cmd_open);
    
	for(byte i=0; i<VALVECOUNT; i++){
    pinMode(valvePins[i], OUTPUT);
    digitalWrite(valvePins[i], LOW);    
  }

  pinMode(POWER_PIN, OUTPUT);
  digitalWrite(POWER_PIN, HIGH);
}

void loop(){
	cmdPoll();	
}
