# Fritzing sketch Controller_B1.0_doubleExtension (saved by Fritzing 0.9.3b)
circuit board: 5.35101cm x 4.04246cm

parts:
  U3 = 74HC595 [package="DIP16 [THT]"]
  ULN2803A = ULN2803A [package=THT]
  J2 = female pin header, 2 pins [form="♀ (female)"]
  J3 = female pin header, 2 pins [form="♀ (female)"]
  J4 = female pin header, 2 pins [form="♀ (female)"]
  J5 = female pin header, 2 pins [form="♀ (female)"]
  J6 = female pin header, 2 pins [form="♀ (female)"]
  J7 = female pin header, 2 pins [form="♀ (female)"]
  J8 = female pin header, 2 pins [form="♀ (female)"]
  J9 = female pin header, 2 pins [form="♀ (female)"]
  U5 = RJ45 Jack [package=rj45-8]
  J10 = female pin header, 2 pins [form="♀ (female)"]
  U7 = 74HC595 [package="DIP16 [THT]"]
  ULN2803A1 = ULN2803A [package=THT]
  U8 = RJ45 Jack [package=rj45-8]
  J11 = female pin header, 2 pins [form="♀ (female)"]
  J12 = female pin header, 2 pins [form="♀ (female)"]
  J13 = female pin header, 2 pins [form="♀ (female)"]
  J14 = female pin header, 2 pins [form="♀ (female)"]
  J15 = female pin header, 2 pins [form="♀ (female)"]
  J16 = female pin header, 2 pins [form="♀ (female)"]
  J17 = female pin header, 2 pins [form="♀ (female)"]
  J18 = female pin header, 2 pins [form="♀ (female)"]
  J19 = female pin header, 2 pins [form="♀ (female)"]

nets:
  N1: U3.Q1, ULN2803A.In_7
  N2: U3.Q2, ULN2803A.In_6
  N3: U3.Q3, ULN2803A.In_5
  N4: U3.Q4, ULN2803A.In_4
  N5: U3.Q5, ULN2803A.In_3
  N6: U3.Q6, ULN2803A.In_2
  N7: U3.Q7, ULN2803A.In_1
  GND: U3.GND, ULN2803A.0V, U5.8, J10.pin2, U7.GND, ULN2803A1.0V, U8.8, J19.pin1
  N8: U3.Q7', U5.4
  VCC: U3.MR, U3.VCC, U5.5, U5.6, U7.MR, U7.VCC, U8.5, U8.6
  N9: U3.SH_CP, U5.2, U7.SH_CP, U8.2
  N10: U3.ST_CP, U5.1, U7.ST_CP, U8.1
  N11: U3.OE, U5.3, U7.OE, U8.3
  N12: U3.DS, U7.Q7'
  N13: U3.Q0, ULN2803A.In_8
  N14: ULN2803A.COM_-_Common, J2.pin1, J3.pin1, J4.pin1, J5.pin1, J6.pin1, J7.pin1, J8.pin1, J9.pin1, U5.7, J10.pin1, ULN2803A1.COM_-_Common, U8.7, J11.pin2, J12.pin2, J13.pin2, J14.pin2, J15.pin2, J16.pin2, J17.pin2, J18.pin2, J19.pin2
  N15: ULN2803A.Out_8, J2.pin2
  N16: ULN2803A.Out_7, J3.pin2
  N17: ULN2803A.Out_6, J4.pin2
  N18: ULN2803A.Out_5, J5.pin2
  N19: ULN2803A.Out_4, J6.pin2
  N20: ULN2803A.Out_3, J7.pin2
  N21: ULN2803A.Out_2, J8.pin2
  N22: ULN2803A.Out_1, J9.pin2
  N23: U7.Q1, ULN2803A1.In_7
  N24: U7.Q2, ULN2803A1.In_6
  N25: U7.Q3, ULN2803A1.In_5
  N26: U7.Q4, ULN2803A1.In_4
  N27: U7.Q5, ULN2803A1.In_3
  N28: U7.Q6, ULN2803A1.In_2
  N29: U7.Q7, ULN2803A1.In_1
  N30: U7.DS, U8.4
  N31: U7.Q0, ULN2803A1.In_8
  N32: ULN2803A1.Out_8, J18.pin1
  N33: ULN2803A1.Out_7, J17.pin1
  N34: ULN2803A1.Out_6, J16.pin1
  N35: ULN2803A1.Out_5, J15.pin1
  N36: ULN2803A1.Out_4, J14.pin1
  N37: ULN2803A1.Out_3, J13.pin1
  N38: ULN2803A1.Out_2, J12.pin1
  N39: ULN2803A1.Out_1, J11.pin1

notes:
  VDC
  GND
  1
  <-
  IsWISaS_Controller_B1.0_extension
  https://github.com/stseeger/IsWISaS
  8
  9
  16
  in
  out
