# Fritzing sketch Controller_B1.0_extension (saved by Fritzing 0.9.3b)
circuit board: 2.80095cm x 5.0061cm

parts:
  U3 = 74HC595 [package="DIP16 [THT]"]
  ULN2803A = ULN2803A [package=THT]
  J2 = female pin header, 2 pins [form="♀ (female)"]
  J3 = female pin header, 2 pins [form="♀ (female)"]
  J4 = female pin header, 2 pins [form="♀ (female)"]
  J5 = female pin header, 2 pins [form="♀ (female)"]
  J6 = female pin header, 2 pins [form="♀ (female)"]
  J7 = female pin header, 2 pins [form="♀ (female)"]
  J8 = female pin header, 2 pins [form="♀ (female)"]
  J9 = female pin header, 2 pins [form="♀ (female)"]
  U5 = RJ45 Jack [package=rj45-8]
  U6 = RJ45 Jack [package=rj45-8]
  J10 = female pin header, 2 pins [form="♀ (female)"]

nets:
  N1: U3.Q1, ULN2803A.In_7
  N2: U3.Q2, ULN2803A.In_6
  N3: U3.Q3, ULN2803A.In_5
  N4: U3.Q4, ULN2803A.In_4
  N5: U3.Q5, ULN2803A.In_3
  N6: U3.Q6, ULN2803A.In_2
  N7: U3.Q7, ULN2803A.In_1
  N8: U3.GND, ULN2803A.0V, U5.8, U6.8, J10.pin2
  N9: U3.Q7', U6.4
  N10: U3.MR, U3.VCC, U5.5, U5.6, U6.5, U6.6
  N11: U3.SH_CP, U5.2, U6.2
  N12: U3.ST_CP, U5.1, U6.1
  N13: U3.OE, U5.3, U6.3
  N14: U3.DS, U5.4
  N15: U3.Q0, ULN2803A.In_8
  N16: ULN2803A.COM_-_Common, J2.pin1, J3.pin1, J4.pin1, J5.pin1, J6.pin1, J7.pin1, J8.pin1, J9.pin1, U5.7, U6.7, J10.pin1
  N17: ULN2803A.Out_8, J2.pin2
  N18: ULN2803A.Out_7, J3.pin2
  N19: ULN2803A.Out_6, J4.pin2
  N20: ULN2803A.Out_5, J5.pin2
  N21: ULN2803A.Out_4, J6.pin2
  N22: ULN2803A.Out_3, J7.pin2
  N23: ULN2803A.Out_2, J8.pin2
  N24: ULN2803A.Out_1, J9.pin2

notes:
  VDC
  GND
  1-8
  -> in
  out ->
  IsWISaS_Controller_B1.0_extension
  https://github.com/stseeger/IsWISaS
