# Fritzing sketch Controller_C1.1 (saved by Fritzing 0.9.3b)
circuit board: 5.32785cm x 5.98431cm
breadboards: 1

parts:
  RX0_TX1 = Arduino Nano (Rev3.0)
  ULN2803A = ULN2803A [package=THT]
  PS/2_port_B2 = mini DIN 6 Connector [package=mini-din6]
  C2 = Electrolytic Capacitor [capacitance=100µF package="100 mil [THT, electrolytic]"]
  R4 = Resistor [tolerance=±5% resistance=100k package=THT]
  R1 = Resistor [tolerance=±5% resistance=3.3k package=THT]
  PS/2_port_B3 = mini DIN 6 Connector [package=mini-din6]
  C1 = Electrolytic Capacitor [capacitance=100µF package="100 mil [THT, electrolytic]"]
  R3 = Resistor [tolerance=±5% resistance=100k package=THT]
  R2 = Resistor [tolerance=±5% resistance=3.3k package=THT]
  J2 = Power Jack [package=power_jack_pth_lock]
  Vreg_12V = Voltage Regulator - 5V [package="TO220 [THT]"]
  U2 = RJ45 Jack [package=rj45-8]
  DI_DE_RE_RO = female pin header, 4 pins [form="♀ (female)"]
  +_B_A_- = female pin header, 4 pins [form="♀ (female)"]
  J3 = double row female pin header, 16 pins [form="♀ (female)"]
  C3 = Tantalum Capacitor [capacitance=330nF voltage=35V package="100 mil [THT, tantalum]"]
  C4 = Ceramic Capacitor [capacitance=100nF package="100 mil [THT, multilayer]"]
  U3 = RJ45 Jack [package=rj45-8]
  J4 = female pin header, 2 pins [form="♀ (female)"]

nets:
  GND: RX0_TX1.GND, ULN2803A.0V, PS/2_port_B2.2, PS/2_port_B2.6, C2.-, R4.Pin_1, PS/2_port_B3.2, PS/2_port_B3.6, C1.-, R3.Pin_1, J2.GND, J2.GNDBREAK, Vreg_12V.GND, U2.3, U2.5, U2.7, +_B_A_-.pin4, C3.-, C4.1, U3.7, J4.pin1
  N1: RX0_TX1.D2, ULN2803A.In_8
  N2: RX0_TX1.D3, ULN2803A.In_7
  N3: RX0_TX1.D4, ULN2803A.In_6
  N4: RX0_TX1.D5, R1.Pin_0
  N5: RX0_TX1.D6, R2.Pin_0
  N6: RX0_TX1.D7, ULN2803A.In_3
  N7: RX0_TX1.D8, ULN2803A.In_2
  N8: RX0_TX1.D9, ULN2803A.In_1
  N9: RX0_TX1.D10, ULN2803A.In_4
  N10: RX0_TX1.D11/MOSI, ULN2803A.In_5
  N11: RX0_TX1.D12/MISO, DI_DE_RE_RO.pin4
  N12: RX0_TX1.5V, +_B_A_-.pin1, U3.6
  N13: RX0_TX1.A7, PS/2_port_B2.5, R4.Pin_0
  N14: RX0_TX1.A6, PS/2_port_B3.5, R3.Pin_0
  N15: RX0_TX1.A5, U3.4
  N16: RX0_TX1.A4, U3.2
  N17: RX0_TX1.A3, U3.1
  N18: RX0_TX1.A2, U3.3
  N19: RX0_TX1.A0, DI_DE_RE_RO.pin1
  N20: RX0_TX1.D13/SCK, DI_DE_RE_RO.pin2, DI_DE_RE_RO.pin3
  N21: ULN2803A.COM_-_Common, PS/2_port_B2.1, PS/2_port_B2.4, PS/2_port_B3.1, PS/2_port_B3.4, Vreg_12V.output_voltage, J3.pin9, J3.pin10, J3.pin11, J3.pin12, J3.pin13, J3.pin14, J3.pin15, J3.pin16, C4.0, U3.8, J4.pin2
  N22: ULN2803A.Out_8, J3.pin8
  N23: ULN2803A.Out_7, J3.pin7
  N24: ULN2803A.Out_6, J3.pin6
  N25: ULN2803A.Out_5, J3.pin5
  N26: ULN2803A.Out_4, J3.pin4
  N27: ULN2803A.Out_3, J3.pin3
  N28: ULN2803A.Out_2, J3.pin2
  N29: ULN2803A.Out_1, J3.pin1
  N30: PS/2_port_B2.3, C2.+, R2.Pin_1
  N31: R1.Pin_1, PS/2_port_B3.3, C1.+
  N32: J2.PWR, Vreg_12V.input_voltage, U2.4, U2.6, U2.8, C3.+
  N33: U2.1, +_B_A_-.pin2
  N34: U2.2, +_B_A_-.pin3

notes:
  +
  12V
  1
  8
  GND
  extension B
  extension C
  IsWISaS_Controller_C1.0
  https://github.com/stseeger/IsWISaS
  MFC_A
  MFC_B

// code stored in the sketch: 16ValveControllerBoard_v1.ino
#include <Cmd.h>

#define POWER_PIN D10
#define VALVECOUNT 16

const byte valvePins[16] = {D2, D3, D4, D5, D6, D7, D8, D9, A7, A6, A5, A4, A3, A2, A1, A0};

byte activeValve = 0;

void identify(int arg_cnt, char **args){
  Serial.print("deviceType:");
  arg_cnt==1 ? Serial.print(' ') : Serial.println();
  Serial.println("ValveController");
}

void cmd_open(int arg_cnt, char **args){
  int valveNumber = cmdStr2Num(args[1], 10);  
  activate(valveNumber);
}

void activate(byte n){
  n = n > 0 & n <=17 ? n : 1;
	activeValve = n;
	Serial.print("open valve ");
	Serial.println(n);
  for(byte i=0; i<VALVECOUNT; i++){
    digitalWrite(valvePins[i], i==(n-1));    
  } 
}

void setup() {
  cmdInit(9600);
  cmdAdd("?", identify);
  cmdAdd("open", cmd_open);
    
	for(byte i=0; i<VALVECOUNT; i++){
    pinMode(valvePins[i], OUTPUT);
    digitalWrite(valvePins[i], LOW);    
  }

  pinMode(POWER_PIN, OUTPUT);
  digitalWrite(POWER_PIN, HIGH);
}

void loop(){
	cmdPoll();	
}
