# Fritzing sketch Controller_C1.2 (saved by Fritzing 0.9.3b)
circuit board: 9.5034cm x 5.95885cm
breadboards: 1

parts:
  RX0_TX1 = Arduino Nano (Rev3.0)
  ULN2803A = ULN2803A [package=THT]
  PS/2_port_B2 = mini DIN 6 Connector [package=mini-din6]
  C2 = Electrolytic Capacitor [capacitance=100µF package="100 mil [THT, electrolytic]"]
  R4 = Resistor [tolerance=±5% resistance=100k package=THT]
  R1 = Resistor [tolerance=±5% resistance=3.3k package=THT]
  PS/2_port_B3 = mini DIN 6 Connector [package=mini-din6]
  C1 = Electrolytic Capacitor [capacitance=100µF package="100 mil [THT, electrolytic]"]
  R3 = Resistor [tolerance=±5% resistance=100k package=THT]
  R2 = Resistor [tolerance=±5% resistance=3.3k package=THT]
  J2 = Power Jack [package=power_jack_pth_lock]
  U2 = RJ45 Jack [package=rj45-8]
  DI_DE_RE_RO = female pin header, 4 pins [form="♀ (female)"]
  +_B_A_- = female pin header, 4 pins [form="♀ (female)"]
  J3 = double row female pin header, 16 pins [form="♀ (female)"]
  J4 = female pin header, 2 pins [form="♀ (female)"]
  U4 = RJ45 Jack [package=rj45-8]
  +_B_A_-_2 = female pin header, 4 pins [form="♀ (female)"]
  DI_DE_RE_RO1 = female pin header, 4 pins [form="♀ (female)"]
  OUT+ = female pin header, 1 pin [form="♀ (female)"]
  IN+ = female pin header, 1 pin [form="♀ (female)"]
  OUT- = female pin header, 1 pin [form="♀ (female)"]
  IN- = female pin header, 1 pin [form="♀ (female)"]
  Vreg_12V = Voltage Regulator - 5V [package="TO220 [THT]"]
  C4 = Tantalum Capacitor [capacitance=330nF voltage=35V package="100 mil [THT, tantalum]"]
  C5 = Ceramic Capacitor [capacitance=100nF package="100 mil [THT, multilayer]"]
  OUT-_IN- = female pin header, 2 pins [form="♀ (female)"]

nets:
  N1: RX0_TX1.GND, ULN2803A.0V, PS/2_port_B2.2, PS/2_port_B2.6, C2.-, R4.Pin_1, PS/2_port_B3.2, PS/2_port_B3.6, C1.-, R3.Pin_1, +_B_A_-.pin4, J4.pin1, +_B_A_-_2.pin4, OUT-.pin1, C5.0, OUT-_IN-.pin1
  N2: RX0_TX1.D2, ULN2803A.In_8
  N3: RX0_TX1.D3, ULN2803A.In_7
  N4: RX0_TX1.D4, ULN2803A.In_6
  N5: RX0_TX1.D5, R1.Pin_0
  N6: RX0_TX1.D6, R2.Pin_0
  N7: RX0_TX1.D7, ULN2803A.In_3
  N8: RX0_TX1.D8, ULN2803A.In_2
  N9: RX0_TX1.D9, ULN2803A.In_1
  N10: RX0_TX1.D10, ULN2803A.In_4
  N11: RX0_TX1.D11/MOSI, ULN2803A.In_5
  N12: RX0_TX1.D12/MISO, DI_DE_RE_RO.pin4, DI_DE_RE_RO1.pin4
  N13: RX0_TX1.5V, +_B_A_-.pin1, +_B_A_-_2.pin1
  N14: RX0_TX1.A7, PS/2_port_B2.5, R4.Pin_0
  N15: RX0_TX1.A6, PS/2_port_B3.5, R3.Pin_0
  N16: RX0_TX1.A0, DI_DE_RE_RO.pin1, DI_DE_RE_RO1.pin1
  N17: RX0_TX1.D13/SCK, DI_DE_RE_RO.pin2, DI_DE_RE_RO.pin3, DI_DE_RE_RO1.pin2, DI_DE_RE_RO1.pin3
  N18: ULN2803A.COM_-_Common, PS/2_port_B2.1, PS/2_port_B2.4, PS/2_port_B3.1, PS/2_port_B3.4, J3.pin9, J3.pin10, J3.pin11, J3.pin12, J3.pin13, J3.pin14, J3.pin15, J3.pin16, J4.pin2, OUT+.pin1, Vreg_12V.output_voltage, C5.1
  N19: ULN2803A.Out_8, J3.pin8
  N20: ULN2803A.Out_7, J3.pin7
  N21: ULN2803A.Out_6, J3.pin6
  N22: ULN2803A.Out_5, J3.pin5
  N23: ULN2803A.Out_4, J3.pin4
  N24: ULN2803A.Out_3, J3.pin3
  N25: ULN2803A.Out_2, J3.pin2
  N26: ULN2803A.Out_1, J3.pin1
  N27: PS/2_port_B2.3, C2.+, R2.Pin_1
  N28: R1.Pin_1, PS/2_port_B3.3, C1.+
  GND: J2.GND, J2.GNDBREAK, U2.3, U2.5, U2.7, U4.3, U4.5, U4.7, IN-.pin1, Vreg_12V.GND, C4.-, OUT-_IN-.pin2
  N29: J2.PWR, U2.4, U2.6, U2.8, U4.4, U4.6, U4.8, IN+.pin1, Vreg_12V.input_voltage, C4.+
  N30: U2.1, +_B_A_-.pin2
  N31: U2.2, +_B_A_-.pin3
  N32: U4.1, +_B_A_-_2.pin2
  N33: U4.2, +_B_A_-_2.pin3

notes:
  +
  12V
  1
  8
  GND
  1st Line
  IsWISaS_Controller_C1.2
  https://github.com/stseeger/IsWISaS
  MFC_A
  MFC_B
  LM2596
  HW-411
  1st MAX485
  2nd MAX485
  2nd Line

// code stored in the sketch: 16ValveControllerBoard_v1.ino
#include <Cmd.h>

#define POWER_PIN D10
#define VALVECOUNT 16

const byte valvePins[16] = {D2, D3, D4, D5, D6, D7, D8, D9, A7, A6, A5, A4, A3, A2, A1, A0};

byte activeValve = 0;

void identify(int arg_cnt, char **args){
  Serial.print("deviceType:");
  arg_cnt==1 ? Serial.print(' ') : Serial.println();
  Serial.println("ValveController");
}

void cmd_open(int arg_cnt, char **args){
  int valveNumber = cmdStr2Num(args[1], 10);  
  activate(valveNumber);
}

void activate(byte n){
  n = n > 0 & n <=17 ? n : 1;
	activeValve = n;
	Serial.print("open valve ");
	Serial.println(n);
  for(byte i=0; i<VALVECOUNT; i++){
    digitalWrite(valvePins[i], i==(n-1));    
  } 
}

void setup() {
  cmdInit(9600);
  cmdAdd("?", identify);
  cmdAdd("open", cmd_open);
    
	for(byte i=0; i<VALVECOUNT; i++){
    pinMode(valvePins[i], OUTPUT);
    digitalWrite(valvePins[i], LOW);    
  }

  pinMode(POWER_PIN, OUTPUT);
  digitalWrite(POWER_PIN, HIGH);
}

void loop(){
	cmdPoll();	
}
