# Fritzing sketch Extension_C1.1 (saved by Fritzing 0.9.3b)
circuit board: 3.75cm x 9.847cm
breadboards: 1

parts:
  U3 = RJ45 Jack [package=rj45-8]
  J5 = female pin header, 2 pins [form="♀ (female)"]
  Bauteil1 = Arduino Pro Mini v13
  5V_B_A_GND = female pin header, 4 pins [form="♀ (female)"]
  DI_DE_RE_RO1 = female pin header, 4 pins [form="♀ (female)"]
  C6 = Ceramic Capacitor [capacitance=100nF package="100 mil [THT, multilayer]"]
  C7 = Tantalum Capacitor [capacitance=330nF voltage=35V package="100 mil [THT, tantalum]"]
  U4 = RJ45 Jack [package=rj45-8]
  ULN2803A1 = ULN2803A [package=THT]
  J6 = double row female pin header, 16 pins [form="♀ (female)"]
  SW4 = DIP Switch 4 Position [package=dipswitch-04]
  3_3k6 = Resistor [tolerance=±5% resistance=68k package=THT]
  3_3k7 = Resistor [tolerance=±5% resistance=33k package=THT]
  3_3k8 = Resistor [tolerance=±5% resistance=15k package=THT]
  3_3k9 = Resistor [tolerance=±5% resistance=6.8k package=THT]
  3_3k10 = Resistor [tolerance=±5% resistance=3.3k package=THT]
  ULN2803A2 = ULN2803A [package=THT]
  J7 = double row female pin header, 16 pins [form="♀ (female)"]
  J8 = female pin header, 2 pins [form="♀ (female)"]
  J9 = female pin header, 11 pins [form="♀ (female)"]
  Vreg_5V = Voltage Regulator - 5V [package="TO220 [THT]"]
  Vreg_12V = Voltage Regulator - 5V [package="TO220 [THT]"]
  C8 = Ceramic Capacitor [capacitance=100nF package="100 mil [THT, multilayer]"]
  J10 = female pin header, 2 pins [form="♀ (female)"]
  J11 = female pin header, 2 pins [form="♀ (female)"]

nets:
  N1: U3.1, 5V_B_A_GND.pin2, U4.1
  N2: U3.2, 5V_B_A_GND.pin3, U4.2
  GND: U3.3, U3.5, U3.7, J5.pin1, Bauteil1.GND, 5V_B_A_GND.pin4, C6.1, C7.-, U4.3, U4.5, U4.7, ULN2803A1.0V, 3_3k10.Pin_1, ULN2803A2.0V, J8.pin1, J9.pin9, Vreg_5V.GND, Vreg_12V.GND, C8.1
  N3: U3.4, U3.6, U3.8, C7.+, U4.4, U4.6, U4.8, Vreg_5V.input_voltage, Vreg_12V.input_voltage
  N4: J5.pin2, C6.0, ULN2803A1.COM_-_Common, J6.pin9, J6.pin10, J6.pin11, J6.pin12, J6.pin13, J6.pin14, J6.pin15, J6.pin16, ULN2803A2.COM_-_Common, J7.pin9, J7.pin10, J7.pin11, J7.pin12, J7.pin13, J7.pin14, J7.pin15, J7.pin16, J8.pin2, J9.pin10, Vreg_12V.output_voltage, J11.pin2
  N5: Bauteil1.D0/TX, DI_DE_RE_RO1.pin1
  N6: Bauteil1.D1/RX, DI_DE_RE_RO1.pin4
  N7: Bauteil1.A4, ULN2803A2.In_8, J9.pin8
  N8: Bauteil1.A5, ULN2803A2.In_7, J9.pin7
  N9: Bauteil1.RAW, J11.pin1
  N10: Bauteil1.VCC, 5V_B_A_GND.pin1, SW4.5, SW4.6, SW4.7, SW4.8, J9.pin11, J10.pin1
  N11: Bauteil1.A3, 3_3k6.Pin_0, 3_3k7.Pin_0, 3_3k8.Pin_0, 3_3k9.Pin_0, 3_3k10.Pin_0
  N12: Bauteil1.A2, ULN2803A2.In_6, J9.pin6
  N13: Bauteil1.A1, ULN2803A2.In_5, J9.pin5
  N14: Bauteil1.A0, ULN2803A2.In_4, J9.pin4
  N15: Bauteil1.D13/SCK, DI_DE_RE_RO1.pin2, DI_DE_RE_RO1.pin3
  N16: Bauteil1.D12/MISO, ULN2803A2.In_3, J9.pin3
  N17: Bauteil1.D11_PWM/MOSI, ULN2803A2.In_2, J9.pin2
  N18: Bauteil1.D10_PWM/SS, ULN2803A2.In_1, J9.pin1
  N19: Bauteil1.D9_PWM, ULN2803A1.In_1
  N20: Bauteil1.D8, ULN2803A1.In_2
  N21: Bauteil1.D7, ULN2803A1.In_3
  N22: Bauteil1.D6_PWM, ULN2803A1.In_4
  N23: Bauteil1.D5_PWM, ULN2803A1.In_5
  N24: Bauteil1.D4, ULN2803A1.In_6
  N25: Bauteil1.D3_PWM, ULN2803A1.In_7
  N26: Bauteil1.D2, ULN2803A1.In_8
  N27: ULN2803A1.Out_8, J6.pin8
  N28: ULN2803A1.Out_7, J6.pin7
  N29: ULN2803A1.Out_6, J6.pin6
  N30: ULN2803A1.Out_5, J6.pin5
  N31: ULN2803A1.Out_4, J6.pin4
  N32: ULN2803A1.Out_3, J6.pin3
  N33: ULN2803A1.Out_2, J6.pin2
  N34: ULN2803A1.Out_1, J6.pin1
  N35: SW4.1, 3_3k9.Pin_1
  N36: SW4.2, 3_3k8.Pin_1
  N37: SW4.3, 3_3k7.Pin_1
  N38: SW4.4, 3_3k6.Pin_1
  N39: ULN2803A2.Out_8, J7.pin8
  N40: ULN2803A2.Out_7, J7.pin7
  N41: ULN2803A2.Out_6, J7.pin6
  N42: ULN2803A2.Out_5, J7.pin5
  N43: ULN2803A2.Out_4, J7.pin4
  N44: ULN2803A2.Out_3, J7.pin3
  N45: ULN2803A2.Out_2, J7.pin2
  N46: ULN2803A2.Out_1, J7.pin1
  N47: Vreg_5V.output_voltage, C8.0, J10.pin2

notes:
  IsWISaS_Extension_C1.1
  https://github.com/stseeger/IsWISaS
  +
  -
  5V 12V GND A4 A5 A2 A1 A0 12 11 10
  5V->VCC
  12V->RAW
