# Fritzing sketch Extension_C1.2 (saved by Fritzing 0.9.3b)
circuit board: 3.77395cm x 7.05441cm
breadboards: 1

parts:
  U3 = RJ45 Jack [package=rj45-8]
  Bauteil1 = Arduino Pro Mini v13
  5V_B_A_GND = female pin header, 4 pins [form="♀ (female)"]
  DI_DE_RE_RO1 = female pin header, 4 pins [form="♀ (female)"]
  C6 = Ceramic Capacitor [capacitance=100nF package="100 mil [THT, multilayer]"]
  C7 = Tantalum Capacitor [capacitance=330nF voltage=35V package="100 mil [THT, tantalum]"]
  U4 = RJ45 Jack [package=rj45-8]
  ULN2803A1 = ULN2803A [package=THT]
  J6 = double row female pin header, 16 pins [form="♀ (female)"]
  SW4 = DIP Switch 4 Position [package=dipswitch-04]
  3_3k6 = Resistor [tolerance=±5% resistance=68k package=THT]
  3_3k7 = Resistor [tolerance=±5% resistance=33k package=THT]
  3_3k8 = Resistor [tolerance=±5% resistance=15k package=THT]
  3_3k9 = Resistor [tolerance=±5% resistance=6.8k package=THT]
  3_3k10 = Resistor [tolerance=±5% resistance=3.3k package=THT]
  Vreg_5V = Voltage Regulator - 5V [package="TO220 [THT]"]
  Vreg_12V = Voltage Regulator - 5V [package="TO220 [THT]"]
  C8 = Ceramic Capacitor [capacitance=100nF package="100 mil [THT, multilayer]"]
  J10 = female pin header, 2 pins [form="♀ (female)"]
  J11 = female pin header, 2 pins [form="♀ (female)"]
  GND_12V_D12_D11_D10_A0 = female pin header, 6 pins [form="♀ (female)"]

nets:
  N1: U3.1, 5V_B_A_GND.pin2, U4.1
  N2: U3.2, 5V_B_A_GND.pin3, U4.2
  GND: U3.3, U3.5, U3.7, Bauteil1.GND, 5V_B_A_GND.pin4, C6.1, C7.-, U4.3, U4.5, U4.7, ULN2803A1.0V, 3_3k10.Pin_1, Vreg_5V.GND, Vreg_12V.GND, C8.1, GND_12V_D12_D11_D10_A0.pin6
  N3: U3.4, U3.6, U3.8, C7.+, U4.4, U4.6, U4.8, Vreg_5V.input_voltage, Vreg_12V.input_voltage
  N4: Bauteil1.D0/TX, DI_DE_RE_RO1.pin1
  N5: Bauteil1.D1/RX, DI_DE_RE_RO1.pin4
  N6: Bauteil1.RAW, J11.pin1
  N7: Bauteil1.VCC, 5V_B_A_GND.pin1, SW4.5, SW4.6, SW4.7, SW4.8, J10.pin1
  N8: Bauteil1.A3, 3_3k6.Pin_0, 3_3k7.Pin_0, 3_3k8.Pin_0, 3_3k9.Pin_0, 3_3k10.Pin_0
  N9: Bauteil1.A0, GND_12V_D12_D11_D10_A0.pin1
  N10: Bauteil1.D13/SCK, DI_DE_RE_RO1.pin2, DI_DE_RE_RO1.pin3
  N11: Bauteil1.D12/MISO, GND_12V_D12_D11_D10_A0.pin4
  N12: Bauteil1.D11_PWM/MOSI, GND_12V_D12_D11_D10_A0.pin3
  N13: Bauteil1.D10_PWM/SS, GND_12V_D12_D11_D10_A0.pin2
  N14: Bauteil1.D9_PWM, ULN2803A1.In_1
  N15: Bauteil1.D8, ULN2803A1.In_2
  N16: Bauteil1.D7, ULN2803A1.In_3
  N17: Bauteil1.D6_PWM, ULN2803A1.In_4
  N18: Bauteil1.D5_PWM, ULN2803A1.In_5
  N19: Bauteil1.D4, ULN2803A1.In_6
  N20: Bauteil1.D3_PWM, ULN2803A1.In_7
  N21: Bauteil1.D2, ULN2803A1.In_8
  N22: C6.0, ULN2803A1.COM_-_Common, J6.pin9, J6.pin10, J6.pin11, J6.pin12, J6.pin13, J6.pin14, J6.pin15, J6.pin16, Vreg_12V.output_voltage, J11.pin2, GND_12V_D12_D11_D10_A0.pin5
  N23: ULN2803A1.Out_8, J6.pin8
  N24: ULN2803A1.Out_7, J6.pin7
  N25: ULN2803A1.Out_6, J6.pin6
  N26: ULN2803A1.Out_5, J6.pin5
  N27: ULN2803A1.Out_4, J6.pin4
  N28: ULN2803A1.Out_3, J6.pin3
  N29: ULN2803A1.Out_2, J6.pin2
  N30: ULN2803A1.Out_1, J6.pin1
  N31: SW4.1, 3_3k9.Pin_1
  N32: SW4.2, 3_3k8.Pin_1
  N33: SW4.3, 3_3k7.Pin_1
  N34: SW4.4, 3_3k6.Pin_1
  N35: Vreg_5V.output_voltage, C8.0, J10.pin2

notes:
  IsWISaS_Extension_C1.2
  https://github.com/stseeger/IsWISaS
  +
  -
  5V->VCC
  12V->RAW
