# Fritzing sketch Extension_C1.3. (saved by Fritzing 0.9.9b)
circuit board: 7.4656cm x 11.0585cm
breadboards: 1

parts:
  U3 = RJ45 Jack [package=rj45-8]
  Bauteil1 = Arduino Pro Mini v13
  5V_B_A_GND = female pin header, 4 pins [form="♀ (female)"]
  DI_DE_RE_RO1 = female pin header, 4 pins [form="♀ (female)"]
  C6 = Ceramic Capacitor [capacitance=100nF package="100 mil [THT, multilayer]"]
  C7 = Tantalum Capacitor [capacitance=330nF voltage=35V package="100 mil [THT, tantalum]"]
  U4 = RJ45 Jack [package=rj45-8]
  SW4 = DIP Switch 4 Position [package=dipswitch-04]
  3_3k6 = Resistor [tolerance=±5% resistance=68k power=0.25 package=THT]
  3_3k7 = Resistor [tolerance=±5% resistance=33k power=0.25 package=THT]
  3_3k8 = Resistor [tolerance=±5% resistance=15k power=0.25 package=THT]
  3_3k9 = Resistor [tolerance=±5% resistance=6.8k power=0.25 package=THT]
  3_3k10 = Resistor [tolerance=±5% resistance=3.3k power=0.25 package=THT]
  Vreg_5V = Voltage Regulator - 5V [package="TO220 [THT]"]
  Vreg_12V = Voltage Regulator - 5V [package="TO220 [THT]"]
  C8 = Ceramic Capacitor [capacitance=100nF package="100 mil [THT, multilayer]"]
  J10 = female pin header, 2 pins [form="♀ (female)"]
  J11 = female pin header, 2 pins [form="♀ (female)"]
  ULN2803A2 = ULN2803A [package=THT]
  ULN2803A3 = ULN2803A [package=THT]
  ULN2803A4 = ULN2803A [package=THT]
  ULN2803A5 = ULN2803A [package=THT]
  ULN2803A6 = ULN2803A [package=THT]
  J16 = double row female pin header, 16 pins [form="♀ (female)"]
  LED29 = LED - 3mm [color="Red (633nm)" current=0.030 package="3 mm [THT]"]
  LED25 = LED - 3mm [color="Red (633nm)" current=0.030 package="3 mm [THT]"]
  LED26 = LED - 3mm [color="Red (633nm)" current=0.030 package="3 mm [THT]"]
  LED30 = LED - 3mm [color="Red (633nm)" current=0.030 package="3 mm [THT]"]
  LED31 = LED - 3mm [color="Red (633nm)" current=0.030 package="3 mm [THT]"]
  LED27 = LED - 3mm [color="Red (633nm)" current=0.030 package="3 mm [THT]"]
  LED32 = LED - 3mm [color="Red (633nm)" current=0.030 package="3 mm [THT]"]
  LED28 = LED - 3mm [color="Red (633nm)" current=0.030 package="3 mm [THT]"]
  J17 = double row female pin header, 16 pins [form="♀ (female)"]
  LED33 = LED - 3mm [color="Red (633nm)" current=0.030 package="3 mm [THT]"]
  LED34 = LED - 3mm [color="Red (633nm)" current=0.030 package="3 mm [THT]"]
  LED35 = LED - 3mm [color="Red (633nm)" current=0.030 package="3 mm [THT]"]
  LED36 = LED - 3mm [color="Red (633nm)" current=0.030 package="3 mm [THT]"]
  LED37 = LED - 3mm [color="Red (633nm)" current=0.030 package="3 mm [THT]"]
  LED38 = LED - 3mm [color="Red (633nm)" current=0.030 package="3 mm [THT]"]
  LED39 = LED - 3mm [color="Red (633nm)" current=0.030 package="3 mm [THT]"]
  LED40 = LED - 3mm [color="Red (633nm)" current=0.030 package="3 mm [THT]"]
  J18 = double row female pin header, 16 pins [form="♀ (female)"]
  LED41 = LED - 3mm [color="Red (633nm)" current=0.030 package="3 mm [THT]"]
  LED42 = LED - 3mm [color="Red (633nm)" current=0.030 package="3 mm [THT]"]
  LED43 = LED - 3mm [color="Red (633nm)" current=0.030 package="3 mm [THT]"]
  LED44 = LED - 3mm [color="Red (633nm)" current=0.030 package="3 mm [THT]"]
  LED45 = LED - 3mm [color="Red (633nm)" current=0.030 package="3 mm [THT]"]
  LED46 = LED - 3mm [color="Red (633nm)" current=0.030 package="3 mm [THT]"]
  LED47 = LED - 3mm [color="Red (633nm)" current=0.030 package="3 mm [THT]"]
  LED48 = LED - 3mm [color="Red (633nm)" current=0.030 package="3 mm [THT]"]
  J19 = double row female pin header, 16 pins [form="♀ (female)"]
  LED49 = LED - 3mm [color="Red (633nm)" current=0.030 package="3 mm [THT]"]
  LED50 = LED - 3mm [color="Red (633nm)" current=0.030 package="3 mm [THT]"]
  LED51 = LED - 3mm [color="Red (633nm)" current=0.030 package="3 mm [THT]"]
  LED52 = LED - 3mm [color="Red (633nm)" current=0.030 package="3 mm [THT]"]
  LED53 = LED - 3mm [color="Red (633nm)" current=0.030 package="3 mm [THT]"]
  LED54 = LED - 3mm [color="Red (633nm)" current=0.030 package="3 mm [THT]"]
  LED55 = LED - 3mm [color="Red (633nm)" current=0.030 package="3 mm [THT]"]
  LED56 = LED - 3mm [color="Red (633nm)" current=0.030 package="3 mm [THT]"]
  R1 = Resistor [tolerance=±5% power=0.25 resistance=220 package=THT]

nets:
  N1: U3.1, 5V_B_A_GND.pin2, U4.1
  N2: U3.2, 5V_B_A_GND.pin3, U4.2
  GND: U3.3, U3.5, U3.7, Bauteil1.GND, 5V_B_A_GND.pin4, C6.1, C7.-, U4.3, U4.5, U4.7, 3_3k10.Pin_1, Vreg_5V.GND, Vreg_12V.GND, C8.1, ULN2803A2.0V
  N3: U3.4, U3.6, U3.8, C7.+, U4.4, U4.6, U4.8, Vreg_5V.input_voltage, Vreg_12V.input_voltage
  N4: Bauteil1.D0/TX, DI_DE_RE_RO1.pin1
  N5: Bauteil1.D1/RX, DI_DE_RE_RO1.pin4
  N6: Bauteil1.VCC, 5V_B_A_GND.pin1, SW4.5, SW4.6, SW4.7, SW4.8, J10.pin1, ULN2803A2.COM_-_Common
  N7: Bauteil1.RAW, J11.pin1
  N8: Bauteil1.A3, 3_3k6.Pin_0, 3_3k7.Pin_0, 3_3k8.Pin_0, 3_3k9.Pin_0, 3_3k10.Pin_0
  N9: Bauteil1.A0, ULN2803A2.In_1
  N10: Bauteil1.D13/SCK, DI_DE_RE_RO1.pin2, DI_DE_RE_RO1.pin3
  N11: Bauteil1.D12/MISO, ULN2803A2.In_2
  N12: Bauteil1.D11_PWM/MOSI, ULN2803A2.In_3
  N13: Bauteil1.D10_PWM/SS, ULN2803A2.In_4
  N14: Bauteil1.D9_PWM, ULN2803A3.In_1, ULN2803A4.In_1, ULN2803A5.In_1, ULN2803A6.In_1
  N15: Bauteil1.D8, ULN2803A3.In_2, ULN2803A4.In_2, ULN2803A5.In_2, ULN2803A6.In_2
  N16: Bauteil1.D7, ULN2803A3.In_3, ULN2803A4.In_3, ULN2803A5.In_3, ULN2803A6.In_3
  N17: Bauteil1.D6_PWM, ULN2803A3.In_4, ULN2803A4.In_4, ULN2803A5.In_4, ULN2803A6.In_4
  N18: Bauteil1.D5_PWM, ULN2803A3.In_5, ULN2803A4.In_5, ULN2803A5.In_5, ULN2803A6.In_5
  N19: Bauteil1.D4, ULN2803A3.In_6, ULN2803A4.In_6, ULN2803A5.In_6, ULN2803A6.In_6
  N20: Bauteil1.D3_PWM, ULN2803A3.In_7, ULN2803A4.In_7, ULN2803A5.In_7, ULN2803A6.In_7
  N21: Bauteil1.D2, ULN2803A3.In_8, ULN2803A4.In_8, ULN2803A5.In_8, ULN2803A6.In_8
  N22: C6.0, Vreg_12V.output_voltage, J11.pin2, ULN2803A3.COM_-_Common, ULN2803A4.COM_-_Common, ULN2803A5.COM_-_Common, ULN2803A6.COM_-_Common, J16.pin1, J16.pin2, J16.pin3, J16.pin4, J16.pin5, J16.pin6, J16.pin7, J16.pin8, J17.pin1, J17.pin2, J17.pin3, J17.pin4, J17.pin5, J17.pin6, J17.pin7, J17.pin8, J18.pin1, J18.pin2, J18.pin3, J18.pin4, J18.pin5, J18.pin6, J18.pin7, J18.pin8, J19.pin1, J19.pin2, J19.pin3, J19.pin4, J19.pin5, J19.pin6, J19.pin7, J19.pin8, R1.Pin_1
  N23: SW4.1, 3_3k9.Pin_1
  N24: SW4.2, 3_3k8.Pin_1
  N25: SW4.3, 3_3k7.Pin_1
  N26: SW4.4, 3_3k6.Pin_1
  N27: Vreg_5V.output_voltage, C8.0, J10.pin2
  N28: ULN2803A2.Out_4, ULN2803A3.0V
  N29: ULN2803A2.Out_3, ULN2803A4.0V
  N30: ULN2803A2.Out_2, ULN2803A5.0V
  N31: ULN2803A2.Out_1, ULN2803A6.0V
  N32: ULN2803A3.Out_8, J19.pin16, LED49.cathode
  N33: ULN2803A3.Out_7, J19.pin15, LED54.cathode
  N34: ULN2803A3.Out_6, J19.pin14, LED55.cathode
  N35: ULN2803A3.Out_5, J19.pin13, LED53.cathode
  N36: ULN2803A3.Out_4, J19.pin12, LED51.cathode
  N37: ULN2803A3.Out_3, J19.pin11, LED50.cathode
  N38: ULN2803A3.Out_2, J19.pin10, LED56.cathode
  N39: ULN2803A3.Out_1, J19.pin9, LED52.cathode
  N40: ULN2803A4.Out_8, J18.pin16, LED41.cathode
  N41: ULN2803A4.Out_7, J18.pin15, LED46.cathode
  N42: ULN2803A4.Out_6, J18.pin14, LED47.cathode
  N43: ULN2803A4.Out_5, J18.pin13, LED45.cathode
  N44: ULN2803A4.Out_4, J18.pin12, LED43.cathode
  N45: ULN2803A4.Out_3, J18.pin11, LED42.cathode
  N46: ULN2803A4.Out_2, J18.pin10, LED48.cathode
  N47: ULN2803A4.Out_1, J18.pin9, LED44.cathode
  N48: ULN2803A5.Out_8, J17.pin16, LED33.cathode
  N49: ULN2803A5.Out_7, J17.pin15, LED38.cathode
  N50: ULN2803A5.Out_6, J17.pin14, LED39.cathode
  N51: ULN2803A5.Out_5, J17.pin13, LED37.cathode
  N52: ULN2803A5.Out_4, J17.pin12, LED35.cathode
  N53: ULN2803A5.Out_3, J17.pin11, LED34.cathode
  N54: ULN2803A5.Out_2, J17.pin10, LED40.cathode
  N55: ULN2803A5.Out_1, J17.pin9, LED36.cathode
  N56: ULN2803A6.Out_8, J16.pin16, LED25.cathode
  N57: ULN2803A6.Out_7, J16.pin15, LED30.cathode
  N58: ULN2803A6.Out_6, J16.pin14, LED32.cathode
  N59: ULN2803A6.Out_5, J16.pin13, LED28.cathode
  N60: ULN2803A6.Out_4, J16.pin12, LED29.cathode
  N61: ULN2803A6.Out_3, J16.pin11, LED26.cathode
  N62: ULN2803A6.Out_2, J16.pin10, LED31.cathode
  N63: ULN2803A6.Out_1, J16.pin9, LED27.cathode
  N64: LED29.anode, LED25.anode, LED26.anode, LED30.anode, LED31.anode, LED27.anode, LED32.anode, LED28.anode, LED33.anode, LED34.anode, LED35.anode, LED36.anode, LED37.anode, LED38.anode, LED39.anode, LED40.anode, LED41.anode, LED42.anode, LED43.anode, LED44.anode, LED45.anode, LED46.anode, LED47.anode, LED48.anode, LED49.anode, LED50.anode, LED51.anode, LED52.anode, LED53.anode, LED54.anode, LED55.anode, LED56.anode, R1.Pin_0

notes:
  IsWISaS_Extension_C1.2
  https://github.com/stseeger/IsWISaS
  5V->VCC
  12V->RAW
  420Ω
