# Fritzing sketch Extra_Extension_C1.2 (saved by Fritzing 0.9.3b)
circuit board: 2.38117cm x 1.92877cm
breadboards: 1

parts:
  Q1 = Basic FET N-Channel [package="TO220 [THT]"]
  Q2 = Basic FET N-Channel [package="TO220 [THT]"]
  J1 = female pin header, 4 pins [form="♀ (female)"]
  J2 = female pin header, 2 pins [form="♀ (female)"]
  J3 = female pin header, 2 pins [form="♀ (female)"]
  D1 = Diode [package=diode-1n4148]
  D2 = Diode [package=diode-1n4148]
  R2 = Resistor [tolerance=±5% resistance=20k package=THT]
  R3 = Resistor [tolerance=±5% resistance=20k package=THT]

nets:
  N1: Q1.gate, Q2.gate, J1.pin4, R2.Pin_0, R3.Pin_0
  N2: Q1.drain, J3.pin2, D1.A
  N3: Q1.source, J1.pin2, R3.Pin_1
  N4: Q2.drain, J2.pin2, D2.A
  N5: Q2.source, J1.pin1, R2.Pin_1
  N6: J1.pin3, J2.pin1, J3.pin1, D1.C, D2.C

notes:
  GND
  12V
  I1
  I2
  O1
  O2
