# Fritzing sketch extension_a1.0 (saved by Fritzing 0.9.3b)
circuit board: 7.92023cm x 1.74045cm
breadboards: 1

parts:
  J1 = double row female pin header, 16 pins [form="♀ (female)"]
  1 = female pin header, 3 pins [form="♀ (female)"]
  2 = female pin header, 3 pins [form="♀ (female)"]
  3 = female pin header, 3 pins [form="♀ (female)"]
  4 = female pin header, 3 pins [form="♀ (female)"]
  5 = female pin header, 3 pins [form="♀ (female)"]
  6 = female pin header, 3 pins [form="♀ (female)"]
  7 = female pin header, 3 pins [form="♀ (female)"]
  8 = female pin header, 3 pins [form="♀ (female)"]
  LED10 = LED - 3mm [color="Green (565nm)" package="3 mm [THT]"]
  LED11 = LED - 3mm [color="Green (565nm)" package="3 mm [THT]"]
  LED12 = LED - 3mm [color="Green (565nm)" package="3 mm [THT]"]
  LED13 = LED - 3mm [color="Green (565nm)" package="3 mm [THT]"]
  LED14 = LED - 3mm [color="Green (565nm)" package="3 mm [THT]"]
  LED15 = LED - 3mm [color="Green (565nm)" package="3 mm [THT]"]
  LED16 = LED - 3mm [color="Green (565nm)" package="3 mm [THT]"]
  R7 = Resistor [tolerance=±5% resistance=220 package=THT]
  LED9 = LED - 3mm [color="Green (565nm)" package="3 mm [THT]"]

nets:
  N1: J1.pin1, 8.pin1, LED16.cathode
  N2: J1.pin2, 7.pin1, LED15.cathode
  N3: J1.pin3, 6.pin1, LED14.cathode
  N4: J1.pin4, 5.pin1, LED13.cathode
  N5: J1.pin5, 4.pin1, LED12.cathode
  N6: J1.pin6, 3.pin1, LED11.cathode
  N7: J1.pin7, 2.pin1, LED10.cathode
  N8: J1.pin8, 1.pin1, LED9.cathode
  N9: J1.pin9, J1.pin10, J1.pin11, J1.pin12, J1.pin13, J1.pin14, J1.pin15, J1.pin16, 1.pin2, 1.pin3, 2.pin2, 2.pin3, 3.pin2, 3.pin3, 4.pin2, 4.pin3, 5.pin2, 5.pin3, 6.pin2, 6.pin3, 7.pin2, 7.pin3, 8.pin2, 8.pin3, R7.Pin_1
  N10: LED10.anode, LED11.anode, LED12.anode, LED13.anode, LED14.anode, LED15.anode, LED16.anode, R7.Pin_0, LED9.anode

notes:
  VDC
  GND(1-8)
  IsWISaS_extension_a1.0
  https://github.com/stseeger/IsWISaS
  + + -
