# Fritzing sketch extension2_1.0 (saved by Fritzing 0.9.3b)
circuit board: 4cm x 2.47555cm
breadboards: 1

parts:
  12V_GND_A2_A1_A0_12_11_10_NC = female pin header, 9 pins [form="♀ (female)"]
  ULN2803A2 = ULN2803A [package=THT]
  J1 = double row female pin header, 6 pins [form="♀ (female)"]
  J2 = double row female pin header, 6 pins [form="♀ (female)"]
  J3 = double row female pin header, 6 pins [form="♀ (female)"]
  J4 = double row female pin header, 6 pins [form="♀ (female)"]
  J5 = double row female pin header, 6 pins [form="♀ (female)"]
  J6 = double row female pin header, 6 pins [form="♀ (female)"]
  12 = LED - 3mm [color="Red (633nm)" package="3 mm [THT]"]
  11 = LED - 3mm [color="Red (633nm)" package="3 mm [THT]"]
  10 = LED - 3mm [color="Red (633nm)" package="3 mm [THT]"]
  9 = LED - 3mm [color="Red (633nm)" package="3 mm [THT]"]
  R2 = Resistor [tolerance=±5% resistance=220 package=THT]
  13 = LED - 3mm [color="Red (633nm)" package="3 mm [THT]"]
  14 = LED - 3mm [color="Red (633nm)" package="3 mm [THT]"]

nets:
  N1: 12V_GND_A2_A1_A0_12_11_10_NC.pin2, ULN2803A2.In_3
  N2: 12V_GND_A2_A1_A0_12_11_10_NC.pin3, ULN2803A2.In_4
  N3: 12V_GND_A2_A1_A0_12_11_10_NC.pin4, ULN2803A2.In_5
  N4: 12V_GND_A2_A1_A0_12_11_10_NC.pin5, ULN2803A2.In_6
  N5: 12V_GND_A2_A1_A0_12_11_10_NC.pin6, ULN2803A2.In_7
  N6: 12V_GND_A2_A1_A0_12_11_10_NC.pin7, ULN2803A2.In_8
  N7: 12V_GND_A2_A1_A0_12_11_10_NC.pin8, ULN2803A2.0V
  N8: 12V_GND_A2_A1_A0_12_11_10_NC.pin9, ULN2803A2.COM_-_Common, J1.pin4, J1.pin5, J1.pin6, J2.pin4, J2.pin5, J2.pin6, J3.pin4, J3.pin5, J3.pin6, J4.pin4, J4.pin5, J4.pin6, J5.pin1, J5.pin2, J5.pin3, J6.pin4, J6.pin5, J6.pin6, R2.Pin_0
  N9: ULN2803A2.Out_8, J1.pin1, J1.pin2, J1.pin3, 12.cathode
  N10: ULN2803A2.Out_7, J2.pin1, J2.pin2, J2.pin3, 11.cathode
  N11: ULN2803A2.Out_6, J3.pin1, J3.pin2, J3.pin3, 10.cathode
  N12: ULN2803A2.Out_5, J4.pin1, J4.pin2, J4.pin3, 9.cathode
  N13: ULN2803A2.Out_4, J6.pin1, J6.pin2, J6.pin3, 13.cathode
  N14: ULN2803A2.Out_3, J5.pin4, J5.pin5, J5.pin6, 14.cathode
  N15: 12.anode, 11.anode, 10.anode, 9.anode, R2.Pin_1, 13.anode, 14.anode

notes:
  -
  +
  IsWISaS_extension²_1.0
  https://github.com/stseeger/IsWISaS
